# Fritzing sketch Accel (saved by Fritzing 0.9.1b)
breadboards: 2

parts:
  Lid_Conn1 = RaspberrySTEM Lid Connector
  IC3 = Accelerometer [chip_label=?]

nets:
  N1: Lid_Conn1.pin1, IC3.pin1
  N2: Lid_Conn1.pin3, IC3.pin3
  N3: Lid_Conn1.pin5, IC3.pin2
  N4: Lid_Conn1.pin_39, IC3.pin4

notes:
  top-left
  top-right
  bottom-left
  bot
