# Fritzing sketch Breadboard_short (saved by Fritzing 0.9.1b)
breadboards: 2

parts:
  Lid_Conn1 = RaspberrySTEM Lid Connector
  R2 = Resistor [tolerance=±5% resistance=100 power=100 package=THT]
  LED1 = LED - 5mm [color="Red (633nm)" package="5 mm [THT]"]

nets:
  N1: Lid_Conn1.pin1, Lid_Conn1.pin_39, R2.Pin_1, LED1.cathode
  N2: R2.Pin_0, LED1.anode

notes:
  top-left
  top-right
  bottom-left
  bot
