# Fritzing sketch Flashlight (saved by Fritzing 0.9.1b)
breadboards: 2

parts:
  Lid_Conn1 = RaspberrySTEM Lid Connector
  R2 = Resistor [tolerance=±5% resistance=100 package=THT]
  LED1 = LED - 5mm [color="Red (633nm)" package="5 mm [THT]"]
  S1 = Pushbutton [package="[THT]"]

nets:
  N1: Lid_Conn1.pin1, R2.Pin_1
  N2: Lid_Conn1.pin8, LED1.cathode
  N3: Lid_Conn1.pin_12, S1.Pin_3, S1.Pin_4
  N4: Lid_Conn1.pin_39, S1.Pin_1, S1.Pin_2
  N5: R2.Pin_0, LED1.anode

notes:
  top-left
  top-right
  bottom-left
  bot
