# Fritzing sketch Inputs (saved by Fritzing 0.9.1b)
breadboards: 2

parts:
  Lid_Conn1 = RaspberrySTEM Lid Connector

nets:
  N1: Lid_Conn1.pin1, Lid_Conn1.pin8
  N2: Lid_Conn1.pin_12, Lid_Conn1.pin_39

notes:
  top-left
  top-right
  bottom-left
  bot
