# Fritzing sketch LED_Matrix_with_ce (saved by Fritzing 0.9.1b)
breadboards: 2

parts:
  Lid_Conn1 = RaspberrySTEM Lid Connector
  IC3 = LED MAtrix [chip_label=IC]

nets:
  N1: Lid_Conn1.pin_39, IC3.pin_10
  N2: IC3.pin1, IC3.pin2
  N3: IC3.pin5, IC3.pin6
  N4: IC3.pin7, IC3.pin8
  N5: IC3.pin_11, IC3.pin_12

notes:
  top-left
  top-right
  bottom-left
  bot
