# Fritzing sketch LED_Matrix_with_ce_and_power (saved by Fritzing 0.9.1b)
breadboards: 2

parts:
  Lid_Conn1 = RaspberrySTEM Lid Connector
  IC2 = LED MAtrix [chip_label=IC]

nets:
  N1: Lid_Conn1.pin1, IC2.pin1, IC2.pin2
  N2: Lid_Conn1.pin_39, IC2.pin5, IC2.pin6, IC2.pin_10
  N3: IC2.pin7, IC2.pin8
  N4: IC2.pin_11, IC2.pin_12

notes:
  top-left
  top-right
  bottom-left
  bot
  For the power-on test, leave these wires disconnected
