# Fritzing sketch Minecraft_4way_2buttons (saved by Fritzing 0.9.1b)
breadboards: 2

parts:
  Lid_Conn1 = RaspberrySTEM Lid Connector
  S1 = Pushbutton [package="[THT]"]
  S2 = Pushbutton [package="[THT]"]
  S3 = Pushbutton [package="[THT]"]
  S4 = Pushbutton [package="[THT]"]
  S5 = Pushbutton [package="[THT]"]
  S6 = Pushbutton [package="[THT]"]

nets:
  N1: Lid_Conn1.pin8, Lid_Conn1.pin_10
  N2: Lid_Conn1.pin_12, S5.Pin_1, S5.Pin_2
  N3: Lid_Conn1.pin_16, S4.Pin_3, S4.Pin_4
  N4: Lid_Conn1.pin_18, S3.Pin_1, S3.Pin_2
  N5: Lid_Conn1.pin_32, S1.Pin_1, S1.Pin_2
  N6: Lid_Conn1.pin_39, S1.Pin_3, S1.Pin_4, S2.Pin_1, S2.Pin_2, S3.Pin_3, S3.Pin_4, S4.Pin_1, S4.Pin_2, S5.Pin_3, S5.Pin_4, S6.Pin_1, S6.Pin_2
  N7: S2.Pin_3, S2.Pin_4
  N8: S6.Pin_3, S6.Pin_4

notes:
  top-left
  top-right
  bottom-left
  bot
