# Fritzing sketch Minecraft_Accel_4way_2buttons (saved by Fritzing 0.9.1b)
breadboards: 2

parts:
  Lid_Conn1 = RaspberrySTEM Lid Connector
  IC3 = Accelerometer [chip_label=?]
  S2 = Pushbutton [package="[THT]"]
  S3 = Pushbutton [package="[THT]"]
  S4 = Pushbutton [package="[THT]"]
  S5 = Pushbutton [package="[THT]"]
  S6 = Pushbutton [package="[THT]"]
  S7 = Pushbutton [package="[THT]"]

nets:
  N1: Lid_Conn1.pin1, IC3.pin1
  N2: Lid_Conn1.pin3, IC3.pin3
  N3: Lid_Conn1.pin5, IC3.pin2
  N4: Lid_Conn1.pin8, Lid_Conn1.pin_10
  N5: Lid_Conn1.pin_12, S5.Pin_1, S5.Pin_2
  N6: Lid_Conn1.pin_16, S4.Pin_3, S4.Pin_4
  N7: Lid_Conn1.pin_18, S3.Pin_1, S3.Pin_2
  N8: Lid_Conn1.pin_26, S7.Pin_1, S7.Pin_2
  N9: Lid_Conn1.pin_39, IC3.pin4, S2.Pin_1, S2.Pin_2, S3.Pin_3, S3.Pin_4, S4.Pin_1, S4.Pin_2, S5.Pin_3, S5.Pin_4, S6.Pin_1, S6.Pin_2, S7.Pin_3, S7.Pin_4
  N10: S2.Pin_3, S2.Pin_4
  N11: S6.Pin_3, S6.Pin_4

notes:
  top-left
  top-right
  bottom-left
  bot
